// Digital circuit piano.dig as structural Verilog
module piano (
  input  clk,
  input  endo,
  input  enre,
  input  enmi,
  input  enfa,
  input  ensol,
  input  enla,
  output [3:0] out
);

  wire clk_divdo, clk_divfa, clk_divla, clk_divmi, clk_divre, clk_divsol, cout, endo_t, enfa_t, eni, enla_t,
       enmi_t, enre_t, ensol_t;
  wire [4:0] counter_7_out;
  wire [31:0] counter_1_out, counter_2_out, counter_3_out, counter_4_out, counter_5_out, counter_6_out;

  Counter #(.Bits(32)) counter_1 (.en(1'b1), .C(clk), .clr(clk_divdo), .out(counter_1_out));  // open: ovf
  Counter #(.Bits(32)) counter_2 (.en(1'b1), .C(clk), .clr(clk_divre), .out(counter_2_out));  // open: ovf
  Counter #(.Bits(32)) counter_3 (.en(1'b1), .C(clk), .clr(clk_divmi), .out(counter_3_out));  // open: ovf
  Counter #(.Bits(32)) counter_4 (.en(1'b1), .C(clk), .clr(clk_divfa), .out(counter_4_out));  // open: ovf
  Counter #(.Bits(32)) counter_5 (.en(1'b1), .C(clk), .clr(clk_divsol), .out(counter_5_out));  // open: ovf
  Counter #(.Bits(32)) counter_6 (.en(1'b1), .C(clk), .clr(clk_divla), .out(counter_6_out));  // open: ovf
  Comparator #(.Bits(32)) comparator_1 (.a(32'hbaa), .b(counter_1_out), .eq(clk_divdo));  // open: gt, lt
  Comparator #(.Bits(32)) comparator_2 (.a(32'ha64), .b(counter_2_out), .eq(clk_divre));  // open: gt, lt
  Comparator #(.Bits(32)) comparator_3 (.a(32'h942), .b(counter_3_out), .eq(clk_divmi));  // open: gt, lt
  Comparator #(.Bits(32)) comparator_4 (.a(32'h8bd), .b(counter_4_out), .eq(clk_divfa));  // open: gt, lt
  Comparator #(.Bits(32)) comparator_5 (.a(32'h7c9), .b(counter_5_out), .eq(clk_divsol));  // open: gt, lt
  Comparator #(.Bits(32)) comparator_6 (.a(32'h6ef), .b(counter_6_out), .eq(clk_divla));  // open: gt, lt
  NoteSelector #(.applicationType("IVERILOG")) u_NoteSelector (
    .cdo(clk_divdo), .cre(clk_divre), .cmi(clk_divmi), .cfa(clk_divfa), .csol(clk_divsol), .cla(clk_divla),
    .bdo(endo_t), .bre(enre_t), .bmi(enmi_t), .bfa(enfa_t), .bsol(ensol_t), .bla(enla_t), .cout(cout),
    .eni(eni));
  Counter #(.Bits(5)) counter_7 (.en(eni), .C(cout), .clr(1'b0), .out(counter_7_out));  // open: ovf
  ROM #(.AddrBits(5), .Bits(4)) rom_1 (.A(counter_7_out), .sel(1'b1), .D(out));
  not not_1 (endo_t, endo);
  not not_2 (enre_t, enre);
  not not_3 (enmi_t, enmi);
  not not_4 (enfa_t, enfa);
  not not_5 (ensol_t, ensol);
  not not_6 (enla_t, enla);

  // Notes on the sheet:
  //   out: Salida 4 bits para DAC, pin H17,J16,K15,L15
  //   clk: pin V10, Hz: 100000000
  //   endo: pin K18
  //   enre: pin K17
  //   enmi: pin L17
  //   enfa: pin M16
  //   ensol: pin L18
  //   enla: pin M18
  //   board:MimasV2
  //   contents of rom_1 (hex, n*v repeats v):
  //   8,9,a,c,d,e,f,f,f,f,e,d,c,b,a,8,7,5,4,3,2,1,0,0,0,0,1,2,3,5,6,8
endmodule

/* Code of NoteSelector:
module NoteSelector
(
    input cdo,
    input cre,
    input cmi,
    input cfa,
    input csol,
    input cla,
    input bdo,
    input bre,
    input bmi,
    input bfa,
    input bsol,
    input bla,
    output reg cout,
    output eni
);

  assign eni = bdo | bre | bmi | bfa | bsol | bla;
  always @ (*) begin
       cout = 1'b0;
       if (bdo) begin
          cout = cdo;
       end
       else if(bre) begin
          cout = cre;
       end
       else if(bmi) begin
          cout = cmi;
       end
       else if(bfa) begin
          cout = cfa;
       end
       else if(bsol) begin
          cout = csol;
       end
       else if(bla) begin
          cout = cla;
       end
  end

endmodule
*/
